# Fritzing sketch WiringDiagram (saved by Fritzing 0.9.3b)
breadboards: 1

parts:
  Part1 = Adafruit Metro M4 Express [part_number="Adafruit #3382"]
  Part2 = Adafruit UDA1334 I2S DAC [part_number="Adafruit #3678"]
  U1 = POT [package=pot_mammoth]

nets:
  N1: Part1.A5, U1.A
  GND: Part1.GND, Part2.GND, U1.S
  N2: Part1.D9, Part2.WORDSEL_IN
  N3: Part1.D8, Part2.DATA_IN
  N4: Part1.D3, Part2.BITCLK_IN
  3.3V: Part1.3.3V, Part2.VIN, U1.E

custom parts:
  Adafruit Metro M4 Express: Are you ready? Really ready? Cause here comes the fastest, most powerful Metro ever. The Adafruit Metro M4 featuring the Microchip ATSAMD51. This Metro is like a bullet train, with it's 120MHz Cortex M4 with floating point support. Your code will zig and zag and zoom, and with a bunch of extra peripherals for support, this will for sure be your favorite new chipset. To start off our ATSAMD51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
  Adafruit UDA1334 I2S DAC: This fully-featured UDA1334A I2S Stereo DAC breakout is a perfect match for any I2S-output audio interface. It's affordable but sounds great! The NXP UDA1334A is a jack-of-all-I2S-trades: you can use 3.3V - 5V logic levels (a rarity), and can process multiple different formats by setting two pins to high or low. The DAC will process data immediately, and give you a clear, analog, stereo line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
